# Fritzing sketch RFID_Project (saved by Fritzing 0.9.3b)
breadboards: 1

parts:
  Orange_Pi_One1 = Orange Pi One [part_number=OPI-ONE]
  KY-1 = Keyes Relay [package=THT]
  Part1 = RFID-RC522-v3
  L1 = Solenoid
  M1 = RioRand LM2596
  LED1 = LED - 5mm [color="Green (565nm)" package="5 mm [THT]"]
  LED2 = LED - 5mm [color="Red (633nm)" package="5 mm [THT]"]
  S1 = Round Pushbutton
  R1 = Resistor [tolerance=±5% resistance=220 package=THT]
  R2 = Resistor [tolerance=±5% resistance=220 package=THT]
  R3 = Resistor [tolerance=±5% resistance=220 package=THT]
  JACK1 = 2.1mm Barrel Jack with Terminal Block

nets:
  3V3: Orange_Pi_One1.3v3, Orange_Pi_One1.3V3, Part1.3.3V, R3.Pin_1
  N1: Orange_Pi_One1.PA6, KY-1.signal
  GND: Orange_Pi_One1.GND, KY-1.ground, Part1.GND, M1.Pin_4, LED1.cathode, LED2.cathode, S1.leg0
  N2: Orange_Pi_One1.PA14, S1.leg1, R3.Pin_0
  N3: Orange_Pi_One1.PA1, R2.Pin_0
  N4: Orange_Pi_One1.PA0, R1.Pin_0
  N5: Orange_Pi_One1.PC0, Part1.MISO
  N6: Orange_Pi_One1.PC1, Part1.MOSI
  N7: Orange_Pi_One1.PC2, Part1.SCK
  N8: Orange_Pi_One1.PC3, Part1.SDA
  N9: Orange_Pi_One1.PA19, Part1.RST
  N10: Orange_Pi_One1.PA7, Part1.IRQ
  N11: Orange_Pi_One1.5V, KY-1.power, M1.Pin_3
  N12: KY-1.C, L1.pin2
  N13: KY-1.NO, M1.Pin_1, JACK1.POS
  N14: L1.pin1, M1.Pin_2, JACK1.NEG
  N15: LED1.anode, R2.Pin_1
  N16: LED2.anode, R1.Pin_1

notes:
  Door Lock
  Input 12V DC
  Door
  Button
  RFID Cards Reader
  System Status LEDS
  DC/DC 5V
  Relay

custom parts:
  Orange Pi One: It’s an open-source single-board computer. It can run Android 4.4, Ubuntu, Debian, Rasberry Pi Image, as well as the banana pi Image. It uses the AllWinner H3 SoC, and has 512MB DDR3 SDRAM
  Keyes Relay: The Keyes 5V relay module is suitable for SCM development, home appliance control. It uses a 5V~12V TIL control signal which can control DC / AC signal.
  RFID-RC522-v3: A simple China made RFID-RC522 Reader (6x4 cm); do check the pin labels, as this is a MFRC522 based clone.
